# Fritzing sketch BH1750 (saved by Fritzing 0.9.6b)

parts:
  Mod1 = Raspberry Pi Pico W
  Part1 = BH1750

nets:
  N1: Mod1.pin_11, Part1.SDA
  N2: Mod1.pin_12, Part1.SCL
  N3: Mod1.pin_33, Mod1.pin_38, Part1.GND
  N4: Mod1.pin_36, Part1.VCC

notes:
  GND
  3.3 V
  GPIO 8
  GPIO 9
  I2C (SDA)
  I2C (SCL)
  Sensor de Intensidad de Luz
  BH1750

custom parts:
  Raspberry Pi Pico W: Raspberry Pi Pico W. Based around the RP2040 microcontroller the Pico W is a low cost microcontroller device bringing Raspberry Pi quality, cost, and easy of use to the microcontroller space. The areas marked KEEPOUT in pcb silkscreen should not have traces running through them to avoid shorts on a soldered in module!
  BH1750: Light Sensor
