# Fritzing sketch DHT22_humedad_temperatura (saved by Fritzing 0.9.6b)

parts:
  Mod1 = Raspberry Pi Pico W
  A1 = DHT22 module

nets:
  N1: Mod1.pin_33, Mod1.pin_38, A1.-
  N2: Mod1.pin_36, A1.+

notes:
  GND
  3.3 V
  GPIO 3
  DIGITAL OUTPUT
  pantalla oled (128x64)
  Raspberry Pi Pico W
  Sensor de Humedad y Temperatura
  DHT22

custom parts:
  Raspberry Pi Pico W: Raspberry Pi Pico W. Based around the RP2040 microcontroller the Pico W is a low cost microcontroller device bringing Raspberry Pi quality, cost, and easy of use to the microcontroller space. The areas marked KEEPOUT in pcb silkscreen should not have traces running through them to avoid shorts on a soldered in module!
  DHT22 module: DHT22 module. Pins VCC Data GND.
