# Fritzing sketch MQ-135 (saved by Fritzing 0.9.6b)

parts:
  Mod1 = Raspberry Pi Pico W
  Mod2 = MQ-135 breakout

nets:
  N1: Mod1.pin_32, Mod2.AO
  N2: Mod1.pin_36, Mod2.VCC
  N3: Mod1.pin_38, Mod1.pin_42, Mod2.GND

notes:
  GND
  3.3 V
  ANALOG
  OUTPUT
  MQ-135
  Sensor de Calidad del aire
  GPIO 27

custom parts:
  Raspberry Pi Pico W: Raspberry Pi Pico W. Based around the RP2040 microcontroller the Pico W is a low cost microcontroller device bringing Raspberry Pi quality, cost, and easy of use to the microcontroller space. The areas marked KEEPOUT in pcb silkscreen should not have traces running through them to avoid shorts on a soldered in module!
  MQ-135 breakout: MQ-135 gas sensor
