# Fritzing sketch Sensor_humedad_suelo (saved by Fritzing 0.9.6b)

parts:
  Mod1 = Raspberry Pi Pico W
  Capacitive_Soil_Moisture_Sensor1 = DFRobot Capacitive Soil Moisture Sensor V1.0 [part_number=SEN0193]

nets:
  N1: Mod1.pin_31, Capacitive_Soil_Moisture_Sensor1.A
  N2: Mod1.pin_33, Mod1.pin_38, Capacitive_Soil_Moisture_Sensor1.GND
  N3: Mod1.pin_36, Capacitive_Soil_Moisture_Sensor1.VCC

notes:
  Sensor de Humedad de Suelo
  GND
  3.3 V
  GPIO 26
  ANALOG OUTPUT
  Raspberry Pi Pico W

custom parts:
  Raspberry Pi Pico W: Raspberry Pi Pico W. Based around the RP2040 microcontroller the Pico W is a low cost microcontroller device bringing Raspberry Pi quality, cost, and easy of use to the microcontroller space. The areas marked KEEPOUT in pcb silkscreen should not have traces running through them to avoid shorts on a soldered in module!
  DFRobot Capacitive Soil Moisture Sensor V1.0: DFRobot Capacitive Soil Moisture Sensor V1.0 This product measures soil moisture levels by capacitive sensing, rather than resistive sensing like other types of moisture sensor. It is made of a corrosion resistant material giving it a long service life. Insert it into soil and impress your friends with the real-time soil moisture data! The product includes an on-board voltage regulator which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
