# Fritzing sketch bateria_li_ion (saved by Fritzing 0.9.6b)

parts:
  Mod1 = Raspberry Pi Pico W
  BAT1 = 18650 battery holder [package=battery-18650-kit]

nets:
  N1: Mod1.pin_33, Mod1.pin_38, BAT1.+

notes:
  GND
  3.7 V
  Batería Li-ion 9800 mAh

custom parts:
  Raspberry Pi Pico W: Raspberry Pi Pico W. Based around the RP2040 microcontroller the Pico W is a low cost microcontroller device bringing Raspberry Pi quality, cost, and easy of use to the microcontroller space. The areas marked KEEPOUT in pcb silkscreen should not have traces running through them to avoid shorts on a soldered in module!
  18650 battery holder: 18650 Battery
