# Fritzing sketch conexiones (saved by Fritzing 0.9.6b)

parts:
  Mod1 = Raspberry Pi Pico W
  Capacitive_Soil_Moisture_Sensor1 = DFRobot Capacitive Soil Moisture Sensor V1.0 [part_number=SEN0193]
  A1 = DHT22 module
  OLED_I2C1 = OLED 128x64 I2C Monochrome Display
  Part1 = BH1750
  Mod2 = KY-016 RGB Full Color LED Module [package="Breakout board"]
  Mod3 = KY-016 RGB Full Color LED Module [package="Breakout board"]
  Mod4 = KY-016 RGB Full Color LED Module [package="Breakout board"]
  Mod5 = KY-016 RGB Full Color LED Module [package="Breakout board"]

nets:
  N1: Mod1.pin_1, Mod2.R
  N2: Mod1.pin_2, Mod2.B
  N3: Mod1.pin_5, A1.Out
  N4: Mod1.pin_6, Mod3.R
  N5: Mod1.pin_7, Mod3.B
  N6: Mod1.pin_9, Mod4.R
  N7: Mod1.pin_10, Mod4.B
  N8: Mod1.pin_11, OLED_I2C1.SDA
  N9: Mod1.pin_12, OLED_I2C1.SCK, Part1.SCL
  N10: Mod1.pin_14, Mod5.R
  N11: Mod1.pin_15, Mod5.B
  N12: Mod1.pin_16, Mod2.G
  N13: Mod1.pin_17, Mod3.G
  N14: Mod1.pin_19, Mod4.G
  N15: Mod1.pin_20, Mod5.G
  N16: Mod1.pin_31, Capacitive_Soil_Moisture_Sensor1.A
  N17: Mod1.pin_33, Mod1.pin_38, Capacitive_Soil_Moisture_Sensor1.GND
  N18: Capacitive_Soil_Moisture_Sensor1.VCC, A1.+
  VDD: OLED_I2C1.VDD, Part1.VCC
  GND: OLED_I2C1.GND, Part1.GND
  N19: Mod2.-, Mod3.-, Mod4.-, Mod5.-

notes:
  Sensor de Humedad de Suelo
  GND
  3.7 V
  GPIO 26
  ANALOG OUTPUT
  GPIO 3
  DIGITAL OUTPUT
  GPIO 8
  GPIO 9
  I2C (SDA)
  I2C (SCL)
  BH1750
  pantalla oled (128x64)
  Sensor de Humedad y Temperatura
  DHT22
  Sensor de Intensidad de Luz
  LEDS RGB
  TEMPERATURA
  HUMEDAD
  LUMINOSIDAD
  AMBIENTE
  SUELO

custom parts:
  Raspberry Pi Pico W: Raspberry Pi Pico W. Based around the RP2040 microcontroller the Pico W is a low cost microcontroller device bringing Raspberry Pi quality, cost, and easy of use to the microcontroller space. The areas marked KEEPOUT in pcb silkscreen should not have traces running through them to avoid shorts on a soldered in module!
  DFRobot Capacitive Soil Moisture Sensor V1.0: DFRobot Capacitive Soil Moisture Sensor V1.0 This product measures soil moisture levels by capacitive sensing, rather than resistive sensing like other types of moisture sensor. It is made of a corrosion resistant material giving it a long service life. Insert it into soil and impress your friends with the real-time soil moisture data! The product includes an on-board voltage regulator which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
  DHT22 module: DHT22 module. Pins VCC Data GND.
  BH1750: Light Sensor
  KY-016 RGB Full Color LED Module: KY-016 Arduino full color 5mm RGB LED, different colors can be obtained by mixing the three primary colors.
