# Fritzing sketch leds_rgb (saved by Fritzing 0.9.6b)

parts:
  Mod1 = Raspberry Pi Pico W
  Mod2 = KY-016 RGB Full Color LED Module [package="Breakout board"]
  Mod3 = KY-016 RGB Full Color LED Module [package="Breakout board"]
  Mod4 = KY-016 RGB Full Color LED Module [package="Breakout board"]
  Mod5 = KY-016 RGB Full Color LED Module [package="Breakout board"]

nets:
  N1: Mod1.pin_1, Mod2.R
  N2: Mod1.pin_2, Mod2.B
  N3: Mod1.pin_6, Mod3.R
  N4: Mod1.pin_7, Mod3.B
  N5: Mod1.pin_9, Mod4.R
  N6: Mod1.pin_10, Mod4.B
  N7: Mod1.pin_14, Mod5.R
  N8: Mod1.pin_15, Mod5.B
  N9: Mod1.pin_16, Mod2.G
  N10: Mod1.pin_17, Mod3.G
  N11: Mod1.pin_19, Mod4.G
  N12: Mod1.pin_20, Mod5.G
  N13: Mod1.pin_33, Mod1.pin_38, Mod2.-, Mod3.-, Mod4.-, Mod5.-

notes:
  GND
  LEDS RGB
  TEMPERATURA
  HUMEDAD
  LUMINOSIDAD
  AMBIENTE
  SUELO

custom parts:
  Raspberry Pi Pico W: Raspberry Pi Pico W. Based around the RP2040 microcontroller the Pico W is a low cost microcontroller device bringing Raspberry Pi quality, cost, and easy of use to the microcontroller space. The areas marked KEEPOUT in pcb silkscreen should not have traces running through them to avoid shorts on a soldered in module!
  KY-016 RGB Full Color LED Module: KY-016 Arduino full color 5mm RGB LED, different colors can be obtained by mixing the three primary colors.
