# Fritzing sketch oled_i2c_168x64 (saved by Fritzing 0.9.6b)

parts:
  Mod1 = Raspberry Pi Pico W
  OLED_I2C1 = OLED 128x64 I2C Monochrome Display

nets:
  N1: Mod1.pin_11, OLED_I2C1.SDA
  N2: Mod1.pin_12, OLED_I2C1.SCK
  N3: Mod1.pin_33, Mod1.pin_38, OLED_I2C1.GND
  N4: Mod1.pin_36, OLED_I2C1.VDD

notes:
  GND
  3.3 V
  GPIO 8
  GPIO 9
  I2C (SDA)
  I2C (SCL)
  pantalla oled (128x64)

custom parts:
  Raspberry Pi Pico W: Raspberry Pi Pico W. Based around the RP2040 microcontroller the Pico W is a low cost microcontroller device bringing Raspberry Pi quality, cost, and easy of use to the microcontroller space. The areas marked KEEPOUT in pcb silkscreen should not have traces running through them to avoid shorts on a soldered in module!
